// Logisim project IT012_Lab01_25520280.circ as structural Verilog: 5 circuits, main circuit TN1
module TN1 (
  input  A,
  input  B,
  input  C,
  output NOT,
  output AND,
  output OR,
  output NAND,
  output NOR,
  output XOR,
  output XNOR,
  output XOR3,
  output NAND3,
  output CHAIN
);

  not not_1 (NOT, A);
  and and_1 (AND, A, B);
  or or_1 (OR, A, B);
  nand nand_1 (NAND, A, B);
  nor nor_1 (NOR, A, B);
  xor xor_1 (XOR, A, B);
  xnor xnor_1 (XNOR, A, B);
  ExactlyOne xor_2 (.out(XOR3), .in0(A), .in1(B), .in2(C));
  nand nand_2 (NAND3, A, B, C);
  nand nand_3 (CHAIN, NAND, C);
endmodule

module TN2 (
  input  X,
  input  Y,
  input  Z,
  output EQi1,
  output EQi2,
  output EQi3,
  output EQi4,
  output EQi5
);

  wire not_1_out, not_2_out, x___x_prime_y_out, x___y___x___z_out, x___y_out, x___y_z_out, x___z_out,
       x_prime_y_out, x_prime_y_prime_out, x_y__prime_2_out, x_y__prime_out, y_z_out;

  not not_1 (not_1_out, X);
  not not_2 (not_2_out, Y);
  and y_z (y_z_out, Y, Z);
  or x___y (x___y_out, X, Y);
  or x___z (x___z_out, X, Z);
  and x_prime_y (x_prime_y_out, not_1_out, Y);
  nor x_y__prime (x_y__prime_out, X, Y);
  and x_prime_y_prime (x_prime_y_prime_out, not_1_out, not_2_out);
  nand x_y__prime_2 (x_y__prime_2_out, X, Y);
  or x___y_z (x___y_z_out, X, y_z_out);
  and x___y___x___z (x___y___x___z_out, x___y_out, x___z_out);
  or x___x_prime_y (x___x_prime_y_out, X, x_prime_y_out);
  xnor xnor_1 (EQi1, x_y__prime_out, x_prime_y_prime_out);
  xnor xnor_2 (EQi2, x_y__prime_2_out, x_prime_y_prime_out);
  xnor xnor_3 (EQi3, x___y_z_out, x___y___x___z_out);
  xnor xnor_4 (EQi5, x___x_prime_y_out, x___y_out);
  xnor xnor_5 (EQi4, x___x_prime_y_out, X);
endmodule

module TN3 (
  input  A,
  input  B,
  input  C,
  input  D,
  output F
);

  wire m2_out, m3_out, m5_out, m7_out, m11_out, m13_out, not_1_out, not_2_out, not_3_out, not_4_out;

  not not_1 (not_1_out, A);
  not not_2 (not_2_out, B);
  not not_3 (not_3_out, C);
  not not_4 (not_4_out, D);
  and m2 (m2_out, not_1_out, not_2_out, C, not_4_out);
  and m3 (m3_out, not_1_out, not_2_out, C, D);
  and m5 (m5_out, not_1_out, B, not_3_out, D);
  and m7 (m7_out, not_1_out, B, C, D);
  and m11 (m11_out, A, not_2_out, C, D);
  and m13 (m13_out, A, B, not_3_out, D);
  or SoP (F, m2_out, m3_out, m5_out, m7_out, m11_out, m13_out);
endmodule

module TN4 (
  input  A,
  input  B,
  input  C,
  input  D,
  output F_can,
  output EQ1,
  output EQ2,
  output F_sop,
  output F_pos
);

  wire A_prime_B_prime_C_out, A_prime_B_prime_C_prime_out, A_prime_C_D_out, A_prime_D_out, B_C_out,
       B_C_prime_D_out, B_prime_C_D_out, B_prime_D_out, C_D_out, m2_out, m3_out, m5_out, m7_out, m11_out,
       m13_out, not_1_out, not_2_out, not_3_out, not_4_out;

  not not_1 (not_1_out, A);
  not not_2 (not_2_out, B);
  not not_3 (not_3_out, C);
  not not_4 (not_4_out, D);
  and m2 (m2_out, not_1_out, not_2_out, C, not_4_out);
  and m3 (m3_out, not_1_out, not_2_out, C, D);
  and m5 (m5_out, not_1_out, B, not_3_out, D);
  and m7 (m7_out, not_1_out, B, C, D);
  and m11 (m11_out, A, not_2_out, C, D);
  and m13 (m13_out, A, B, not_3_out, D);
  and A_prime_B_prime_C (A_prime_B_prime_C_out, not_1_out, not_2_out, C);
  and A_prime_C_D (A_prime_C_D_out, not_1_out, C, D);
  and B_C_prime_D (B_C_prime_D_out, B, not_3_out, D);
  and B_prime_C_D (B_prime_C_D_out, not_2_out, C, D);
  or C_D (C_D_out, C, D);
  or B_C (B_C_out, B, C);
  or A_prime_D (A_prime_D_out, not_1_out, D);
  or B_prime_D (B_prime_D_out, not_2_out, D);
  or A_prime_B_prime_C_prime (A_prime_B_prime_C_prime_out, not_1_out, not_2_out, not_3_out);
  and and_1 (F_pos, C_D_out, B_C_out, A_prime_D_out, B_prime_D_out, A_prime_B_prime_C_prime_out);
  or SoP (F_can, m2_out, m3_out, m5_out, m7_out, m11_out, m13_out);
  or SoP_2 (F_sop, A_prime_B_prime_C_out, A_prime_C_D_out, B_C_prime_D_out, B_prime_C_D_out);
  xnor xnor_1 (EQ1, F_can, F_sop);
  xnor xnor_2 (EQ2, F_can, F_pos);
endmodule

module TN5 (
  input  A,
  input  B,
  input  C,
  output F
);

  wire xor_1_out;

  xor xor_1 (xor_1_out, A, B);
  xor xor_2 (F, xor_1_out, C);
endmodule
