// Logisim project IT012_Lab01_25520280_TN2.circ as structural Verilog: 1 circuit, main circuit main
module main (
  input  X,
  input  Y,
  input  Z,
  output EQi1,
  output EQi2,
  output EQi3,
  output EQi4,
  output EQi5
);

  wire not_1_out, not_2_out, x___x_prime_y_out, x___y___x___z_out, x___y_out, x___y_z_out, x___z_out,
       x_prime_y_out, x_prime_y_prime_out, x_y__prime_2_out, x_y__prime_out, y_z_out;

  not not_1 (not_1_out, X);
  not not_2 (not_2_out, Y);
  and y_z (y_z_out, Y, Z);
  or x___y (x___y_out, X, Y);
  or x___z (x___z_out, X, Z);
  and x_prime_y (x_prime_y_out, not_1_out, Y);
  nor x_y__prime (x_y__prime_out, X, Y);
  and x_prime_y_prime (x_prime_y_prime_out, not_1_out, not_2_out);
  nand x_y__prime_2 (x_y__prime_2_out, X, Y);
  or x___y_z (x___y_z_out, X, y_z_out);
  and x___y___x___z (x___y___x___z_out, x___y_out, x___z_out);
  or x___x_prime_y (x___x_prime_y_out, X, x_prime_y_out);
  xnor xnor_1 (EQi1, x_y__prime_out, x_prime_y_prime_out);
  xnor xnor_2 (EQi2, x_y__prime_2_out, x_prime_y_prime_out);
  xnor xnor_3 (EQi3, x___y_z_out, x___y___x___z_out);
  xnor xnor_4 (EQi5, x___x_prime_y_out, x___y_out);
  xnor xnor_5 (EQi4, x___x_prime_y_out, X);
endmodule
