// Logisim project IT012_Lab01_25520280_TN3.circ as structural Verilog: 1 circuit, main circuit main
module main (
  input  A,
  input  B,
  input  C,
  input  D,
  output F
);

  wire m2_out, m3_out, m5_out, m7_out, m11_out, m13_out, not_1_out, not_2_out, not_3_out, not_4_out;

  not not_1 (not_1_out, A);
  not not_2 (not_2_out, B);
  not not_3 (not_3_out, C);
  not not_4 (not_4_out, D);
  and m2 (m2_out, not_1_out, not_2_out, C, not_4_out);
  and m3 (m3_out, not_1_out, not_2_out, C, D);
  and m5 (m5_out, not_1_out, B, not_3_out, D);
  and m7 (m7_out, not_1_out, B, C, D);
  and m11 (m11_out, A, not_2_out, C, D);
  and m13 (m13_out, A, B, not_3_out, D);
  or SoP (F, m2_out, m3_out, m5_out, m7_out, m11_out, m13_out);
endmodule
