// Logisim project IT012_Lab01_25520280_TN4.circ as structural Verilog: 1 circuit, main circuit main
module main (
  input  A,
  input  B,
  input  C,
  input  D,
  output F_can,
  output EQ1,
  output EQ2,
  output F_sop,
  output F_pos
);

  wire A_prime_B_prime_C_out, A_prime_B_prime_C_prime_out, A_prime_C_D_out, A_prime_D_out, B_C_out,
       B_C_prime_D_out, B_prime_C_D_out, B_prime_D_out, C_D_out, m2_out, m3_out, m5_out, m7_out, m11_out,
       m13_out, not_1_out, not_2_out, not_3_out, not_4_out;

  not not_1 (not_1_out, A);
  not not_2 (not_2_out, B);
  not not_3 (not_3_out, C);
  not not_4 (not_4_out, D);
  and m2 (m2_out, not_1_out, not_2_out, C, not_4_out);
  and m3 (m3_out, not_1_out, not_2_out, C, D);
  and m5 (m5_out, not_1_out, B, not_3_out, D);
  and m7 (m7_out, not_1_out, B, C, D);
  and m11 (m11_out, A, not_2_out, C, D);
  and m13 (m13_out, A, B, not_3_out, D);
  and A_prime_B_prime_C (A_prime_B_prime_C_out, not_1_out, not_2_out, C);
  and A_prime_C_D (A_prime_C_D_out, not_1_out, C, D);
  and B_C_prime_D (B_C_prime_D_out, B, not_3_out, D);
  and B_prime_C_D (B_prime_C_D_out, not_2_out, C, D);
  or C_D (C_D_out, C, D);
  or B_C (B_C_out, B, C);
  or A_prime_D (A_prime_D_out, not_1_out, D);
  or B_prime_D (B_prime_D_out, not_2_out, D);
  or A_prime_B_prime_C_prime (A_prime_B_prime_C_prime_out, not_1_out, not_2_out, not_3_out);
  and and_1 (F_pos, C_D_out, B_C_out, A_prime_D_out, B_prime_D_out, A_prime_B_prime_C_prime_out);
  or SoP (F_can, m2_out, m3_out, m5_out, m7_out, m11_out, m13_out);
  or SoP_2 (F_sop, A_prime_B_prime_C_out, A_prime_C_D_out, B_C_prime_D_out, B_prime_C_D_out);
  xnor xnor_1 (EQ1, F_can, F_sop);
  xnor xnor_2 (EQ2, F_can, F_pos);
endmodule
